// Logisim project JK FLIP FLOP.circ as structural Verilog: 1 circuit, main circuit main
module main (
  input  J,
  input  K,
  output Q_prime,
  output Q
);

  wire and_1_out, and_2_out, clock_1_out;

  Clock clock_1 (.out(clock_1_out));
  and and_1 (and_1_out, Q_prime, J, clock_1_out);
  and and_2 (and_2_out, clock_1_out, K, Q);
  nor nor_1 (Q_prime, and_1_out, Q);
  nor nor_2 (Q, Q_prime, and_2_out);

  // Notes on the sheet:
  //   SR FLIP FLOP
  //   JK FLIP FLOP
endmodule
