// Logisim project SR and D FLIP FLOP.circ as structural Verilog: 1 circuit, main circuit main
module main (
  input  S,
  input  R,
  input  D,
  output out_4,
  output out_5,
  output out_6,
  output out_7
);

  wire and_1_out, and_2_out, and_3_out, and_4_out, clock_1_out, clock_2_out, not_1_out, or_1_out, or_2_out,
       or_3_out, or_4_out;

  Clock clock_1 (.out(clock_1_out));
  Clock clock_2 (.out(clock_2_out));
  not not_1 (not_1_out, D);
  and and_1 (and_1_out, S, clock_1_out);
  and and_2 (and_2_out, clock_1_out, R);
  and and_3 (and_3_out, not_1_out, clock_2_out);
  and and_4 (and_4_out, clock_2_out, D);
  or or_1 (or_1_out, and_1_out, out_5);
  or or_2 (or_2_out, out_4, and_2_out);
  or or_3 (or_3_out, and_3_out, out_7);
  or or_4 (or_4_out, out_6, and_4_out);
  not not_2 (out_4, or_1_out);
  not not_3 (out_5, or_2_out);
  not not_4 (out_6, or_3_out);
  not not_5 (out_7, or_4_out);

  // Notes on the sheet:
  //   D FLip FLOP
  //   SR FLIP FLOP
endmodule
